# Fritzing sketch MQ2 (saved by Fritzing 0.9.2b)
breadboards: 1

parts:
  Componente1 = Arduino Uno (Rev3)
  Componente2 = MQ-9 breakout
  LED1 = LED - 5mm [color="Red (633nm)" package="5 mm [THT]"]
  R1 = Resistor [tolerance=±5% resistance=220 package="0805 [SMD]"]
  R2 = Resistor [tolerance=±5% resistance=220 package="0805 [SMD]"]
  LED2 = LED - 5mm [color="Green (570nm)" package="5 mm [THT]"]
  J1 = Piezo Speaker

nets:
  N1: Componente1.A0, Componente2.AO
  N2: Componente1.D2, Componente2.DO
  N3: Componente1.D3_PWM, LED2.anode
  N4: Componente1.D4, LED1.anode
  5V: Componente1.5V, Componente2.VCC, J1.pin2
  GND: Componente1.GND, Componente2.GND, R1.Pin_1, R2.Pin_1, J1.pin1
  N5: LED1.cathode, R2.Pin_0
  N6: R1.Pin_0, LED2.cathode

custom parts:
  MQ-9 breakout: SKU: 101284
